// Logisim project CN.circ as structural Verilog: 1 circuit, main circuit main
module main (
  input  [1:0] in_1,
  input  in_2,
  input  [7:0] in_3,
  input  in_4,
  input  [7:0] in_5
);

  wire and_2_out, and_3_out, and_4_out, and_5_out, and_6_out, END_FLAG, multiplexer_15_out, N0, not_1_out,
       not_4_out, NOT_A8, NOT_S0, NOT_S1, Q_1, SIGN_Q_FINAL, START, SUB, TARGET_REACHED, WE_M, WE_OUT,
       xor_2_out, xor_3_out;
  wire [0:0] SRT2_Q;
  wire [1:0] CU_SIGNAL, Q, SELECT_M, xor_1_out;
  wire [3:0] counter_1_q, multiplexer_22_out;
  wire [5:0] BOOTH_Q;
  wire [7:0] A_DIV, A_IN_F, B_IN_F, FINAL_A, FINAL_Q, M, multiplexer_10_out, multiplexer_13_out,
       multiplexer_14_out, multiplexer_19_out, negator_1_out, negator_3_out, negator_4_out, Q_DIV, Q_SHIFTED;
  wire [8:0] A, A_NEG_REMAINDER, A_SHIFTED, ADDER_RESULT, ALU_IN_A, bit_extender_1_out, bit_extender_2_out,
       bit_extender_3_out, bit_extender_4_out, bit_extender_5_out, BOOTH_A, multiplexer_1_out,
       multiplexer_2_out, multiplexer_8_out, multiplexer_9_out, negator_2_out, shifter_1_out, xor_4_out;
  wire [8:8] multiplexer_6_out;
  wire [15:0] multiplexer_12_out, RES_ADD_SUB;

  Multiplexer #(.select(2), .width(9)) multiplexer_1 (
    .in0(A), .in1({9{1'b0}}), .in2(A), .in3(A_SHIFTED), .out(multiplexer_1_out));  // open: sel
  assign bit_extender_1_out = {{1{1'b0}}, M};  // Bit_Extender bit_extender_1
  assign bit_extender_2_out = {{1{M[7]}}, M};  // Bit_Extender bit_extender_2
  xor xor_1 (xor_1_out[0], Q[0], Q_1);
  assign bit_extender_3_out = {{1{1'b0}}, M};  // Bit_Extender bit_extender_3
  Negator negator_1 (.in({BOOTH_Q, Q}), .out(negator_1_out));
  Register #(.width(9)) u_A (.D(multiplexer_1_out), .en(CU_SIGNAL[0]), .clk(in_2), .Q(A), .clr(in_4));
  Multiplexer #(.select(2), .width(9)) multiplexer_2 (
    .in0(bit_extender_2_out), .in1(bit_extender_2_out), .in2(bit_extender_2_out), .in3(bit_extender_1_out),
    .out(multiplexer_2_out), .sel(in_1));
  Shifter #(.width(9)) shifter_1 (.in(bit_extender_2_out), .\dist (4'b0001), .out(shifter_1_out));
  Multiplexer #(.select(2)) multiplexer_3 (.in0(1'b0), .in1(1'b1), .in2(Q[1]), .in3(NOT_A8), .out(SUB));  // open: sel
  xor xor_2 (xor_2_out, Q[1], Q[0]);
  xor xor_3 (xor_3_out, Q[0], Q_1);
  Adder #(.width(9)) adder_1 (.a(A), .b(bit_extender_3_out), .out(A_NEG_REMAINDER));  // open: cin, cout
  Multiplexer #(.width(8)) multiplexer_4 (.in0({BOOTH_Q, Q}), .in1(negator_1_out), .out(Q_DIV), .sel(SIGN_Q_FINAL));
  Multiplexer #(.select(2), .width(8)) multiplexer_5 (
    .in0({BOOTH_Q, Q}), .in1({BOOTH_Q, Q}), .in2({BOOTH_Q, Q}), .in3(Q_DIV), .out(FINAL_Q), .sel(in_1));
  Multiplexer #(.width(9)) multiplexer_6 (
    .in0(A_NEG_REMAINDER), .in1(negator_2_out), .out({multiplexer_6_out[8], A_DIV}), .sel(NOT_A8));
  Negator #(.width(9)) negator_2 (.in(A), .out(negator_2_out));
  Multiplexer #(.select(2), .width(8)) multiplexer_7 (
    .in0(A[7:0]), .in1(A[7:0]), .in2(A[7:0]), .in3(A_DIV), .out(FINAL_A), .sel(in_1));
  assign bit_extender_4_out = {{8{SUB}}, SUB};  // Bit_Extender bit_extender_4
  Multiplexer #(.select(2), .width(9)) multiplexer_8 (
    .in0({9{1'b0}}), .in1(multiplexer_2_out), .in2(shifter_1_out), .in3({9{1'b0}}), .out(multiplexer_8_out),
    .sel(SELECT_M));
  and and_1 (xor_1_out[1], xor_2_out, not_1_out);
  not not_1 (not_1_out, xor_3_out);
  assign xor_4_out = bit_extender_4_out ^ multiplexer_8_out;  // XOR_Gate xor_4, 9 bits wide
  Multiplexer #(.select(2), .width(9)) multiplexer_9 (
    .in0(bit_extender_5_out), .in1(bit_extender_5_out), .in2(ALU_IN_A), .in3(ALU_IN_A),
    .out(multiplexer_9_out), .sel(in_1));
  assign bit_extender_5_out = {{1{BOOTH_Q[5]}}, {BOOTH_Q, Q}};  // Bit_Extender bit_extender_5
  Register u_Q (.D(multiplexer_10_out), .en(CU_SIGNAL[0]), .clk(in_2), .Q({BOOTH_Q, Q}), .clr(in_4));
  Multiplexer #(.select(2), .width(8)) multiplexer_10 (
    .in0({BOOTH_Q, Q}), .in1(A_IN_F), .in2({BOOTH_Q, Q}), .in3(Q_SHIFTED), .out(multiplexer_10_out));  // open: sel
  Adder #(.width(9)) adder_2 (.a(xor_4_out), .b(multiplexer_9_out), .out(ADDER_RESULT), .cin(SUB));  // open: cout
  Multiplexer #(.select(2), .width(2)) multiplexer_11 (
    .in0(2'b01), .in1(2'b01), .in2(xor_1_out), .in3(2'b01), .out(SELECT_M));  // open: sel
  assign RES_ADD_SUB = {{8{FINAL_A[7]}}, FINAL_A};  // Bit_Extender bit_extender_6
  Multiplexer #(.width(16)) multiplexer_12 (
    .in0(RES_ADD_SUB), .in1({FINAL_A, FINAL_Q}), .out(multiplexer_12_out), .sel(in_1[1]));
  Negator negator_3 (.in(in_3), .out(negator_3_out));
  Negator negator_4 (.in(in_5), .out(negator_4_out));
  Register #(.width(16)) OUT_PUT (.D(multiplexer_12_out), .en(WE_OUT), .clk(in_2), .clr(in_4));  // open: Q
  Multiplexer #(.width(8)) multiplexer_13 (.in0(in_3), .in1(negator_3_out), .out(multiplexer_13_out), .sel(in_3[7]));
  Multiplexer #(.width(8)) multiplexer_14 (.in0(in_5), .in1(negator_4_out), .out(multiplexer_14_out), .sel(in_5[7]));
  Register #(.width(1)) u_Q_1 (.D(multiplexer_15_out), .en(CU_SIGNAL[0]), .clk(in_2), .Q(Q_1), .clr(in_4));
  Multiplexer #(.select(2)) multiplexer_15 (
    .in0(Q_1), .in1(1'b0), .in2(Q_1), .in3(Q[1]), .out(multiplexer_15_out));  // open: sel
  not not_2 (SRT2_Q[0], ADDER_RESULT[8]);
  Shifter #(.shift("ar"), .width(9)) shifter_2 (.in(ADDER_RESULT), .\dist (4'b0010), .out(BOOTH_A));
  Multiplexer #(.select(2), .width(9)) multiplexer_16 (
    .in0(A), .in1(A), .in2(A), .in3({A[7:0], BOOTH_Q[5]}), .out(ALU_IN_A), .sel(in_1));
  Multiplexer #(.select(2), .width(8)) multiplexer_17 (
    .in0(in_3), .in1(in_3), .in2(in_3), .in3(multiplexer_13_out), .out(A_IN_F));  // open: sel
  Multiplexer #(.select(2), .width(8)) multiplexer_18 (
    .in0(in_5), .in1(in_5), .in2(in_5), .in3(multiplexer_14_out), .out(B_IN_F));  // open: sel
  Multiplexer #(.select(2), .width(8)) multiplexer_19 (
    .in0(M), .in1(B_IN_F), .in2(M), .in3(M), .out(multiplexer_19_out));  // open: sel
  Register u_M (.D(multiplexer_19_out), .en(WE_M), .clk(in_2), .Q(M), .clr(in_4));
  not not_3 (NOT_A8, A[7]);
  xor xor_5 (SIGN_Q_FINAL, in_3[7], in_5[7]);
  Multiplexer #(.select(2), .width(9)) multiplexer_20 (
    .in0(ADDER_RESULT), .in1(ADDER_RESULT), .in2(BOOTH_A), .in3(ADDER_RESULT), .out(A_SHIFTED));  // open: sel
  Multiplexer #(.select(2), .width(8)) multiplexer_21 (
    .in0({BOOTH_Q, Q}), .in1({BOOTH_Q, Q}), .in2({ADDER_RESULT[1:0], BOOTH_Q}),
    .in3({BOOTH_Q[4:0], Q, SRT2_Q[0]}), .out(Q_SHIFTED), .sel(in_1));
  Button u_START (.out(START));
  Counter #(.max('hf), .width(4)) counter_1 (
    .clr(and_2_out), .up(1'b1), .count(and_3_out), .clk(in_2), .Q(counter_1_q));  // open: load, D, carry
  and and_2 (and_2_out, NOT_S1, CU_SIGNAL[0]);
  and and_3 (and_3_out, CU_SIGNAL[1], CU_SIGNAL[0]);
  Register #(.width(2)) FSM_STATE (.D({CU_SIGNAL[0], N0}), .en(1'b1), .clk(in_2), .Q(CU_SIGNAL), .clr(in_4));
  not not_4 (not_4_out, TARGET_REACHED);
  Multiplexer #(.select(2), .width(4)) multiplexer_22 (
    .in0(4'b0000), .in1(4'b0000), .in2(4'b0011), .in3(4'b0111), .out(multiplexer_22_out), .sel(in_1));
  and and_4 (and_4_out, NOT_S1, NOT_S0, START);
  and and_5 (and_5_out, NOT_S1, CU_SIGNAL[0]);
  and and_6 (and_6_out, CU_SIGNAL[1], CU_SIGNAL[0], not_4_out);
  Comparator #(.mode("unsigned"), .width(4)) comparator_1 (
    .a(counter_1_q), .b(multiplexer_22_out), .eq(TARGET_REACHED));  // open: gt, lt
  not not_5 (NOT_S0, CU_SIGNAL[0]);
  not not_6 (NOT_S1, CU_SIGNAL[1]);
  and and_7 (WE_M, CU_SIGNAL[0], NOT_S1);
  and and_8 (END_FLAG, NOT_S0, CU_SIGNAL[1]);
  and and_9 (WE_OUT, CU_SIGNAL[1], NOT_S0);
  or or_1 (N0, and_4_out, and_5_out, and_6_out);

  // Other names for the same wires on the sheet: HOLD_A[8:0] = A; A_IN[7:0] = in_3; SIGN_A_IN = in_3[7];
  //   BOOTH_Q[7:6] = ADDER_RESULT[1:0]; B_IN[7:0] = in_5; SIGN_B_IN = in_5[7]; CLK = in_2; N1 = CU_SIGNAL[0];
  //   S0 = CU_SIGNAL[0]; WE_A = CU_SIGNAL[0]; WE_Q = CU_SIGNAL[0]; S1 = CU_SIGNAL[1]; OPCODE[1:0] = in_1;
  //   Q[7:2] = BOOTH_Q; RES_MUL_DIV[15:0] = {FINAL_A, FINAL_Q}; RST = in_4; SRT2_Q[7:1] = {BOOTH_Q[4:0], Q}

  // Notes on the sheet:
  //   2*M(M << 1)
  //   SELECT_M[0]
  //   Non-Restoring Division Correction
  //   0;M;2M;Don't care
  //   ADD OR SUBSTRACT SELECT_M?
  //   SELECT 0, M OR 2*M?
  //   Non-Restoring only works with positive numbers
  //   BOOTH RADIX4 SHIFT
  //   SRT2 PRE-SHIFT
  //   SRT2 SHIFT Q
  //   Select the shift operation result
endmodule
